// Logisim project 4bit-computer.circ as structural Verilog: 20 circuits, main circuit main
module main (
  input  in_1,
  input  in_2,
  input  in_3,
  input  in_4,
  input  in_5,
  input  in_6,
  input  in_7,
  input  in_8,
  input  in_9,
  input  in_10,
  input  in_11,
  input  in_12,
  input  in_13,
  input  in_14
);

  wire alu_1_out_10, alu_1_out_11, alu_1_out_12, alu_1_out_13, memory_1_out_10, memory_1_out_11,
       memory_1_out_12, memory_1_out_13, n7_segment_display_2_a, n7_segment_display_2_b,
       n7_segment_display_2_c, n7_segment_display_2_d, n7_segment_display_2_e, n7_segment_display_2_f,
       n7_segment_display_2_g, n7_segment_display_2_h, n7_segment_display_6_a, n7_segment_display_6_b,
       n7_segment_display_6_c, n7_segment_display_6_d, n7_segment_display_6_e, n7_segment_display_6_f,
       n7_segment_display_6_g, n7_segment_display_6_h, n7_segment_display_9_a, n7_segment_display_9_b,
       n7_segment_display_9_c, n7_segment_display_9_d, n7_segment_display_9_e, n7_segment_display_9_f,
       n7_segment_display_9_g, n7_segment_display_9_h, n7_segment_display_10_a, n7_segment_display_10_b,
       n7_segment_display_10_c, n7_segment_display_10_d, n7_segment_display_10_e, n7_segment_display_10_f,
       n7_segment_display_10_g, n7_segment_display_10_h, not_1_out, not_2_out;

  _7_Segment_Display_part u_7_segment_display_1 (.g(n7_segment_display_2_h));  // open: f, a, b, e, d, c, dp
  _7_Segment_Display u_7_segment_display_2 (
    .in_1(in_2), .in_2(in_3), .in_3(in_4), .in_4(in_5), .A(n7_segment_display_2_a),
    .B(n7_segment_display_2_b), .C(n7_segment_display_2_c), .D(n7_segment_display_2_d),
    .E(n7_segment_display_2_e), .F(n7_segment_display_2_f), .G(n7_segment_display_2_g),
    .H(n7_segment_display_2_h));
  _7_Segment_Display_part u_7_segment_display_3 (
    .g(n7_segment_display_2_g), .f(n7_segment_display_2_f), .a(n7_segment_display_2_a),
    .b(n7_segment_display_2_b), .e(n7_segment_display_2_e), .d(n7_segment_display_2_d),
    .c(n7_segment_display_2_c));  // open: dp
  _7_Segment_Display_part u_7_segment_display_4 (.g(1'b1), .b(not_2_out), .c(not_1_out));  // open: f, a, e, d, dp
  _7_Segment_Display_part u_7_segment_display_5 (.g(1'b1), .f(not_2_out), .e(not_1_out));  // open: a, b, d, c, dp
  not not_1 (not_1_out, in_1);
  ALU alu_1 (
    .in_5(in_1), .out_10(alu_1_out_10), .out_11(alu_1_out_11), .out_12(alu_1_out_12), .out_13(alu_1_out_13),
    .in_1(in_2), .in_2(in_3), .in_4(in_5), .in_6(in_6), .in_7(in_7), .in_8(in_8), .in_9(in_9), .in_3(in_4));
  Memory memory_1 (
    .in_5(alu_1_out_10), .in_6(alu_1_out_11), .in_7(alu_1_out_12), .in_8(alu_1_out_13), .in_1(in_10),
    .in_2(in_11), .in_3(in_12), .in_4(in_13), .in_9(in_14), .out_10(memory_1_out_10),
    .out_11(memory_1_out_11), .out_12(memory_1_out_12), .out_13(memory_1_out_13));
  _7_Segment_Display u_7_segment_display_6 (
    .in_1(memory_1_out_10), .in_2(memory_1_out_11), .in_3(memory_1_out_12), .in_4(memory_1_out_13),
    .A(n7_segment_display_6_a), .B(n7_segment_display_6_b), .C(n7_segment_display_6_c),
    .D(n7_segment_display_6_d), .E(n7_segment_display_6_e), .F(n7_segment_display_6_f),
    .G(n7_segment_display_6_g), .H(n7_segment_display_6_h));
  not not_2 (not_2_out, in_1);
  _7_Segment_Display_part u_7_segment_display_7 (.g(n7_segment_display_9_h));  // open: f, a, b, e, d, c, dp
  _7_Segment_Display_part u_7_segment_display_8 (
    .g(n7_segment_display_9_g), .f(n7_segment_display_9_f), .a(n7_segment_display_9_a),
    .b(n7_segment_display_9_b), .e(n7_segment_display_9_e), .d(n7_segment_display_9_d),
    .c(n7_segment_display_9_c));  // open: dp
  _7_Segment_Display u_7_segment_display_9 (
    .in_1(in_6), .in_2(in_7), .in_3(in_8), .in_4(in_9), .A(n7_segment_display_9_a),
    .B(n7_segment_display_9_b), .C(n7_segment_display_9_c), .D(n7_segment_display_9_d),
    .E(n7_segment_display_9_e), .F(n7_segment_display_9_f), .G(n7_segment_display_9_g),
    .H(n7_segment_display_9_h));
  _7_Segment_Display u_7_segment_display_10 (
    .in_1(alu_1_out_10), .in_2(alu_1_out_11), .in_3(alu_1_out_12), .in_4(alu_1_out_13),
    .A(n7_segment_display_10_a), .B(n7_segment_display_10_b), .C(n7_segment_display_10_c),
    .D(n7_segment_display_10_d), .E(n7_segment_display_10_e), .F(n7_segment_display_10_f),
    .G(n7_segment_display_10_g), .H(n7_segment_display_10_h));
  _7_Segment_Display_part u_7_segment_display_11 (.g(n7_segment_display_6_h));  // open: f, a, b, e, d, c, dp
  _7_Segment_Display_part u_7_segment_display_12 (
    .g(n7_segment_display_6_g), .f(n7_segment_display_6_f), .a(n7_segment_display_6_a),
    .b(n7_segment_display_6_b), .e(n7_segment_display_6_e), .d(n7_segment_display_6_d),
    .c(n7_segment_display_6_c));  // open: dp
  _7_Segment_Display_part u_7_segment_display_13 (.a(1'b1), .d(1'b1));  // open: g, f, b, e, c, dp
  _7_Segment_Display_part u_7_segment_display_14 (
    .g(n7_segment_display_10_g), .f(n7_segment_display_10_f), .a(n7_segment_display_10_a),
    .b(n7_segment_display_10_b), .e(n7_segment_display_10_e), .d(n7_segment_display_10_d),
    .c(n7_segment_display_10_c));  // open: dp
  _7_Segment_Display_part u_7_segment_display_15 (.g(n7_segment_display_10_h));  // open: f, a, b, e, d, c, dp
endmodule

module Half_Adder (
  input  A,
  input  B,
  output Sum,
  output Carry
);

  and and_1 (Carry, A, B);
  xor xor_1 (Sum, A, B);
endmodule

module Full_Adder (
  input  C,
  input  B,
  input  A,
  output Sum,
  output Carry
);

  wire half_adder_1_carry, half_adder_1_sum, half_adder_2_carry;

  Half_Adder half_adder_1 (.A(B), .B(A), .Sum(half_adder_1_sum), .Carry(half_adder_1_carry));
  Half_Adder half_adder_2 (.A(C), .B(half_adder_1_sum), .Sum(Sum), .Carry(half_adder_2_carry));
  or or_1 (Carry, half_adder_2_carry, half_adder_1_carry);
endmodule

module _4_bit_Sign_Switcher (
  input  in_1,
  input  in_2,
  input  in_3,
  input  in_4,
  input  in_5,
  output out_6,
  output out_7,
  output out_8,
  output out_9
);

  wire xor_1_out, xor_2_out, xor_3_out, xor_4_out;

  xor xor_1 (xor_1_out, in_1, in_2);
  xor xor_2 (xor_2_out, in_1, in_3);
  xor xor_3 (xor_3_out, in_1, in_4);
  xor xor_4 (xor_4_out, in_1, in_5);
  _4_bit_Adder u_4_bit_adder_1 (
    .out_9(out_9), .out_10(out_8), .out_11(out_7), .out_12(out_6), .in_1(1'b0), .in_2(1'b0), .in_3(1'b0),
    .in_4(in_1), .in_5(xor_1_out), .in_6(xor_2_out), .in_7(xor_3_out), .in_8(xor_4_out));
endmodule

module _4_bit_Adder (
  input  in_1,
  input  in_2,
  input  in_3,
  input  in_4,
  input  in_5,
  input  in_6,
  input  in_7,
  input  in_8,
  output out_9,
  output out_10,
  output out_11,
  output out_12
);

  wire full_adder_1_carry, full_adder_2_carry, half_adder_1_carry;

  Half_Adder half_adder_1 (.A(in_4), .B(in_8), .Sum(out_9), .Carry(half_adder_1_carry));
  Full_Adder full_adder_1 (.C(half_adder_1_carry), .B(in_3), .A(in_7), .Sum(out_10), .Carry(full_adder_1_carry));
  Full_Adder full_adder_2 (.C(full_adder_1_carry), .B(in_2), .A(in_6), .Sum(out_11), .Carry(full_adder_2_carry));
  Full_Adder full_adder_3 (.C(full_adder_2_carry), .B(in_1), .A(in_5), .Sum(out_12));  // open: Carry
endmodule

module _7seg_A (
  input  a,
  input  b,
  input  c,
  input  d,
  output out_5
);

  wire and_1_out, and_2_out, and_3_out, and_4_out, and_5_out, not_1_out, not_2_out, not_3_out, not_4_out,
       not_5_out, not_6_out;

  not not_1 (not_1_out, d);
  not not_2 (not_2_out, b);
  not not_3 (not_3_out, d);
  not not_4 (not_4_out, b);
  not not_5 (not_5_out, c);
  not not_6 (not_6_out, a);
  and and_1 (and_1_out, c, not_1_out);
  and and_2 (and_2_out, not_2_out, not_3_out);
  and and_3 (and_3_out, not_4_out, c);
  and and_4 (and_4_out, a, not_5_out, d);
  and and_5 (and_5_out, not_6_out, b, d);
  or or_1 (out_5, and_1_out, and_2_out, and_3_out, and_4_out, and_5_out);
endmodule

module _7seg_B (
  input  a,
  input  b,
  input  c,
  input  d,
  output out_5
);

  wire and_1_out, and_2_out, and_3_out, and_4_out, and_5_out, not_1_out, not_2_out, not_3_out, not_4_out,
       not_5_out;

  not not_1 (not_1_out, a);
  not not_2 (not_2_out, b);
  not not_3 (not_3_out, c);
  not not_4 (not_4_out, d);
  not not_5 (not_5_out, c);
  and and_1 (and_1_out, not_1_out, not_2_out);
  and and_2 (and_2_out, a, b);
  and and_3 (and_3_out, not_3_out, not_4_out);
  and and_4 (and_4_out, a, not_5_out);
  and and_5 (and_5_out, b, c, d);
  or or_1 (out_5, and_1_out, and_2_out, and_3_out, and_4_out, and_5_out);
endmodule

module _7seg_C (
  input  a,
  input  b,
  input  c,
  input  d,
  output out_5
);

  wire and_1_out, and_2_out, not_1_out, not_2_out, not_3_out;

  not not_1 (not_1_out, c);
  not not_2 (not_2_out, a);
  and and_1 (and_1_out, not_2_out, b);
  and and_2 (and_2_out, a, not_3_out);
  not not_3 (not_3_out, b);
  or or_1 (out_5, not_1_out, d, and_1_out, and_2_out);
endmodule

module _7seg_D (
  input  a,
  input  b,
  input  c,
  input  d,
  output out_5
);

  wire and_1_out, and_2_out, and_3_out, and_4_out, not_1_out, not_2_out, not_3_out, not_4_out, not_5_out;

  not not_1 (not_1_out, b);
  not not_2 (not_2_out, d);
  not not_3 (not_3_out, d);
  not not_4 (not_4_out, b);
  not not_5 (not_5_out, c);
  and and_1 (and_1_out, not_1_out, not_2_out);
  and and_2 (and_2_out, c, not_3_out);
  and and_3 (and_3_out, not_4_out, c);
  and and_4 (and_4_out, b, not_5_out, d);
  or or_1 (out_5, and_1_out, and_2_out, and_3_out, and_4_out);
endmodule

module _7seg_E (
  input  a,
  input  b,
  input  c,
  input  d,
  output out_5
);

  wire and_1_out, and_2_out, not_1_out, not_2_out, not_3_out;

  not not_1 (not_1_out, b);
  not not_2 (not_2_out, d);
  not not_3 (not_3_out, d);
  and and_1 (and_1_out, not_1_out, not_2_out);
  and and_2 (and_2_out, c, not_3_out);
  or or_1 (out_5, and_1_out, and_2_out);
endmodule

module _7seg_F (
  input  a,
  input  b,
  input  c,
  input  d,
  output out_5
);

  wire and_1_out, and_2_out, and_3_out, and_4_out, not_1_out, not_2_out, not_3_out, not_4_out, not_5_out,
       not_6_out, not_7_out;

  not not_1 (not_1_out, c);
  not not_2 (not_2_out, d);
  not not_3 (not_3_out, a);
  not not_4 (not_4_out, d);
  not not_5 (not_5_out, b);
  not not_6 (not_6_out, a);
  not not_7 (not_7_out, c);
  and and_1 (and_1_out, not_1_out, not_2_out);
  and and_2 (and_2_out, not_3_out, b, not_4_out);
  and and_3 (and_3_out, a, not_5_out, c);
  and and_4 (and_4_out, not_6_out, b, not_7_out);
  or or_1 (out_5, and_1_out, and_2_out, and_3_out, and_4_out);
endmodule

module _7seg_G (
  input  a,
  input  b,
  input  c,
  input  d,
  output out_5
);

  wire and_1_out, and_2_out, and_3_out, and_4_out, not_1_out, not_2_out, not_3_out, not_4_out;

  not not_1 (not_1_out, b);
  not not_2 (not_2_out, d);
  not not_3 (not_3_out, c);
  not not_4 (not_4_out, d);
  and and_1 (and_1_out, not_1_out, c);
  and and_2 (and_2_out, a, not_2_out);
  and and_3 (and_3_out, b, not_3_out);
  and and_4 (and_4_out, b, not_4_out);
  or or_1 (out_5, and_1_out, and_2_out, and_3_out, and_4_out);
endmodule

module _7seg_H (
  input  a,
  input  b,
  input  c,
  input  d,
  output out_5
);


  assign out_5 = a;
endmodule

module _7_Segment_Display (
  input  in_1,
  input  in_2,
  input  in_3,
  input  in_4,
  output A,
  output B,
  output C,
  output D,
  output E,
  output F,
  output G,
  output H
);

  _7seg_A u_7seg_a_1 (.a(in_1), .b(in_2), .c(in_3), .d(in_4), .out_5(A));
  _7seg_B u_7seg_b_1 (.a(in_1), .b(in_2), .c(in_3), .d(in_4), .out_5(B));
  _7seg_C u_7seg_c_1 (.a(in_1), .b(in_2), .c(in_3), .d(in_4), .out_5(C));
  _7seg_D u_7seg_d_1 (.a(in_1), .b(in_2), .c(in_3), .d(in_4), .out_5(D));
  _7seg_E u_7seg_e_1 (.a(in_1), .b(in_2), .c(in_3), .d(in_4), .out_5(E));
  _7seg_F u_7seg_f_1 (.a(in_1), .b(in_2), .c(in_3), .d(in_4), .out_5(F));
  _7seg_G u_7seg_g_1 (.a(in_1), .b(in_2), .c(in_3), .d(in_4), .out_5(G));
  _7seg_H u_7seg_h_1 (.a(in_1), .b(in_2), .c(in_3), .d(in_4), .out_5(H));
endmodule

module ALU (
  input  in_1,
  input  in_2,
  input  in_3,
  input  in_4,
  input  in_5,
  input  in_6,
  input  in_7,
  input  in_8,
  input  in_9,
  output out_10,
  output out_11,
  output out_12,
  output out_13
);

  wire n4_bit_sign_switcher_1_out_6, n4_bit_sign_switcher_1_out_7, n4_bit_sign_switcher_1_out_8,
       n4_bit_sign_switcher_1_out_9;

  _4_bit_Adder u_4_bit_adder_1 (
    .out_9(out_13), .out_10(out_12), .out_11(out_11), .out_12(out_10), .in_1(in_1), .in_2(in_2), .in_3(in_3),
    .in_4(in_4), .in_5(n4_bit_sign_switcher_1_out_6), .in_6(n4_bit_sign_switcher_1_out_7),
    .in_7(n4_bit_sign_switcher_1_out_8), .in_8(n4_bit_sign_switcher_1_out_9));
  _4_bit_Sign_Switcher u_4_bit_sign_switcher_1 (
    .in_1(in_5), .out_6(n4_bit_sign_switcher_1_out_6), .out_7(n4_bit_sign_switcher_1_out_7),
    .out_8(n4_bit_sign_switcher_1_out_8), .out_9(n4_bit_sign_switcher_1_out_9), .in_2(in_6), .in_3(in_7),
    .in_4(in_8), .in_5(in_9));
endmodule

module Gated_D_Latch (
  input  Data,
  input  Write_Enable,
  output out_3
);

  wire and_1_out, and_2_out, and_3_out, and_4_out, not_1_out, not_2_out, not_4_out;

  and and_1 (and_1_out, Data, Write_Enable);
  and and_2 (and_2_out, not_1_out, Write_Enable);
  not not_1 (not_1_out, and_1_out);
  not not_2 (not_2_out, and_2_out);
  and and_3 (and_3_out, not_1_out, not_4_out);
  and and_4 (and_4_out, out_3, not_2_out);
  not not_3 (out_3, and_3_out);
  not not_4 (not_4_out, and_4_out);
endmodule

module _4_bit_Memory_Cell (
  input  Row,
  input  Write_Enable,
  input  in_3,
  input  in_4,
  input  in_5,
  input  in_6,
  input  Col,
  output out_8,
  output out_9,
  output out_10,
  output out_11
);

  wire and_1_out, gated_d_latch_1_out_3, gated_d_latch_2_out_3, gated_d_latch_3_out_3, gated_d_latch_4_out_3;

  and and_1 (and_1_out, Row, Write_Enable, Col);
  Gated_D_Latch gated_d_latch_1 (.Data(in_3), .Write_Enable(and_1_out), .out_3(gated_d_latch_1_out_3));
  Gated_D_Latch gated_d_latch_2 (.Data(in_4), .Write_Enable(and_1_out), .out_3(gated_d_latch_2_out_3));
  Gated_D_Latch gated_d_latch_3 (.Data(in_5), .Write_Enable(and_1_out), .out_3(gated_d_latch_3_out_3));
  Gated_D_Latch gated_d_latch_4 (.Data(in_6), .Write_Enable(and_1_out), .out_3(gated_d_latch_4_out_3));
  and and_2 (out_9, gated_d_latch_2_out_3, Row, Col);
  and and_3 (out_8, gated_d_latch_1_out_3, Row, Col);
  and and_4 (out_10, gated_d_latch_3_out_3, Row, Col);
  and and_5 (out_11, gated_d_latch_4_out_3, Row, Col);
endmodule

module MemoryRow (
  input  a,
  input  b,
  output out_3,
  output out_4,
  output out_5,
  output out_6
);

  wire not_1_out, not_2_out, not_3_out, not_4_out;

  not not_1 (not_1_out, a);
  not not_2 (not_2_out, b);
  not not_3 (not_3_out, a);
  not not_4 (not_4_out, b);
  and and_1 (out_3, not_1_out, not_2_out);
  and and_2 (out_4, not_3_out, b);
  and and_3 (out_5, a, not_4_out);
  and and_4 (out_6, a, b);
endmodule

module MemoryCol (
  input  c,
  input  d,
  output out_3,
  output out_4,
  output out_5,
  output out_6
);

  wire not_1_out, not_2_out, not_3_out, not_4_out;

  not not_1 (not_1_out, c);
  not not_2 (not_2_out, d);
  not not_3 (not_3_out, c);
  not not_4 (not_4_out, d);
  and and_1 (out_3, not_1_out, not_2_out);
  and and_2 (out_4, not_3_out, d);
  and and_3 (out_5, c, not_4_out);
  and and_4 (out_6, c, d);
endmodule

module Memory (
  input  in_1,
  input  in_2,
  input  in_3,
  input  in_4,
  input  in_5,
  input  in_6,
  input  in_7,
  input  in_8,
  input  in_9,
  output out_10,
  output out_11,
  output out_12,
  output out_13
);

  wire memorycol_1_out_3, memorycol_1_out_4, memorycol_1_out_5, memorycol_1_out_6, memoryrow_1_out_3,
       memoryrow_1_out_4, memoryrow_1_out_5, memoryrow_1_out_6, n4_bit_memory_cell_1_out_8,
       n4_bit_memory_cell_1_out_9, n4_bit_memory_cell_1_out_10, n4_bit_memory_cell_1_out_11,
       n4_bit_memory_cell_2_out_8, n4_bit_memory_cell_2_out_9, n4_bit_memory_cell_2_out_10,
       n4_bit_memory_cell_2_out_11, n4_bit_memory_cell_3_out_8, n4_bit_memory_cell_3_out_9,
       n4_bit_memory_cell_3_out_10, n4_bit_memory_cell_3_out_11, n4_bit_memory_cell_4_out_8,
       n4_bit_memory_cell_4_out_9, n4_bit_memory_cell_4_out_10, n4_bit_memory_cell_4_out_11,
       n4_bit_memory_cell_5_out_8, n4_bit_memory_cell_5_out_9, n4_bit_memory_cell_5_out_10,
       n4_bit_memory_cell_5_out_11, n4_bit_memory_cell_6_out_8, n4_bit_memory_cell_6_out_9,
       n4_bit_memory_cell_6_out_10, n4_bit_memory_cell_6_out_11, n4_bit_memory_cell_7_out_8,
       n4_bit_memory_cell_7_out_9, n4_bit_memory_cell_7_out_10, n4_bit_memory_cell_7_out_11,
       n4_bit_memory_cell_8_out_8, n4_bit_memory_cell_8_out_9, n4_bit_memory_cell_8_out_10,
       n4_bit_memory_cell_8_out_11, n4_bit_memory_cell_9_out_8, n4_bit_memory_cell_9_out_9,
       n4_bit_memory_cell_9_out_10, n4_bit_memory_cell_9_out_11, n4_bit_memory_cell_10_out_8,
       n4_bit_memory_cell_10_out_9, n4_bit_memory_cell_10_out_10, n4_bit_memory_cell_10_out_11,
       n4_bit_memory_cell_11_out_8, n4_bit_memory_cell_11_out_9, n4_bit_memory_cell_11_out_10,
       n4_bit_memory_cell_11_out_11, n4_bit_memory_cell_12_out_8, n4_bit_memory_cell_12_out_9,
       n4_bit_memory_cell_12_out_10, n4_bit_memory_cell_12_out_11, n4_bit_memory_cell_13_out_8,
       n4_bit_memory_cell_13_out_9, n4_bit_memory_cell_13_out_10, n4_bit_memory_cell_13_out_11,
       n4_bit_memory_cell_14_out_8, n4_bit_memory_cell_14_out_9, n4_bit_memory_cell_14_out_10,
       n4_bit_memory_cell_14_out_11, n4_bit_memory_cell_15_out_8, n4_bit_memory_cell_15_out_9,
       n4_bit_memory_cell_15_out_10, n4_bit_memory_cell_15_out_11, n4_bit_memory_cell_16_out_8,
       n4_bit_memory_cell_16_out_9, n4_bit_memory_cell_16_out_10, n4_bit_memory_cell_16_out_11;

  MemoryRow memoryrow_1 (
    .out_3(memoryrow_1_out_3), .out_4(memoryrow_1_out_4), .out_5(memoryrow_1_out_5),
    .out_6(memoryrow_1_out_6), .a(in_1), .b(in_2));
  _4_bit_Memory_Cell u_4_bit_memory_cell_1 (
    .Row(memoryrow_1_out_3), .Write_Enable(in_9), .out_8(n4_bit_memory_cell_1_out_8),
    .out_9(n4_bit_memory_cell_1_out_9), .out_10(n4_bit_memory_cell_1_out_10),
    .out_11(n4_bit_memory_cell_1_out_11), .Col(memorycol_1_out_3), .in_3(in_5), .in_4(in_6), .in_5(in_7),
    .in_6(in_8));
  _4_bit_Memory_Cell u_4_bit_memory_cell_2 (
    .Row(memoryrow_1_out_4), .Write_Enable(in_9), .out_8(n4_bit_memory_cell_2_out_8),
    .out_9(n4_bit_memory_cell_2_out_9), .out_10(n4_bit_memory_cell_2_out_10),
    .out_11(n4_bit_memory_cell_2_out_11), .Col(memorycol_1_out_3), .in_3(in_5), .in_4(in_6), .in_5(in_7),
    .in_6(in_8));
  _4_bit_Memory_Cell u_4_bit_memory_cell_3 (
    .Row(memoryrow_1_out_5), .Write_Enable(in_9), .out_8(n4_bit_memory_cell_3_out_8),
    .out_9(n4_bit_memory_cell_3_out_9), .out_10(n4_bit_memory_cell_3_out_10),
    .out_11(n4_bit_memory_cell_3_out_11), .Col(memorycol_1_out_3), .in_3(in_5), .in_4(in_6), .in_5(in_7),
    .in_6(in_8));
  _4_bit_Memory_Cell u_4_bit_memory_cell_4 (
    .Row(memoryrow_1_out_6), .Write_Enable(in_9), .out_8(n4_bit_memory_cell_4_out_8),
    .out_9(n4_bit_memory_cell_4_out_9), .out_10(n4_bit_memory_cell_4_out_10),
    .out_11(n4_bit_memory_cell_4_out_11), .Col(memorycol_1_out_3), .in_3(in_5), .in_4(in_6), .in_5(in_7),
    .in_6(in_8));
  _4_bit_Memory_Cell u_4_bit_memory_cell_5 (
    .Row(memoryrow_1_out_3), .Write_Enable(in_9), .out_8(n4_bit_memory_cell_5_out_8),
    .out_9(n4_bit_memory_cell_5_out_9), .out_10(n4_bit_memory_cell_5_out_10),
    .out_11(n4_bit_memory_cell_5_out_11), .Col(memorycol_1_out_4), .in_3(in_5), .in_4(in_6), .in_5(in_7),
    .in_6(in_8));
  _4_bit_Memory_Cell u_4_bit_memory_cell_6 (
    .Row(memoryrow_1_out_4), .Write_Enable(in_9), .out_8(n4_bit_memory_cell_6_out_8),
    .out_9(n4_bit_memory_cell_6_out_9), .out_10(n4_bit_memory_cell_6_out_10),
    .out_11(n4_bit_memory_cell_6_out_11), .Col(memorycol_1_out_4), .in_3(in_5), .in_4(in_6), .in_5(in_7),
    .in_6(in_8));
  _4_bit_Memory_Cell u_4_bit_memory_cell_7 (
    .Row(memoryrow_1_out_5), .Write_Enable(in_9), .out_8(n4_bit_memory_cell_7_out_8),
    .out_9(n4_bit_memory_cell_7_out_9), .out_10(n4_bit_memory_cell_7_out_10),
    .out_11(n4_bit_memory_cell_7_out_11), .Col(memorycol_1_out_4), .in_3(in_5), .in_4(in_6), .in_5(in_7),
    .in_6(in_8));
  _4_bit_Memory_Cell u_4_bit_memory_cell_8 (
    .Row(memoryrow_1_out_6), .Write_Enable(in_9), .out_8(n4_bit_memory_cell_8_out_8),
    .out_9(n4_bit_memory_cell_8_out_9), .out_10(n4_bit_memory_cell_8_out_10),
    .out_11(n4_bit_memory_cell_8_out_11), .Col(memorycol_1_out_4), .in_3(in_5), .in_4(in_6), .in_5(in_7),
    .in_6(in_8));
  _4_bit_Memory_Cell u_4_bit_memory_cell_9 (
    .Row(memoryrow_1_out_3), .Write_Enable(in_9), .out_8(n4_bit_memory_cell_9_out_8),
    .out_9(n4_bit_memory_cell_9_out_9), .out_10(n4_bit_memory_cell_9_out_10),
    .out_11(n4_bit_memory_cell_9_out_11), .Col(memorycol_1_out_5), .in_3(in_5), .in_4(in_6), .in_5(in_7),
    .in_6(in_8));
  _4_bit_Memory_Cell u_4_bit_memory_cell_10 (
    .Row(memoryrow_1_out_4), .Write_Enable(in_9), .out_8(n4_bit_memory_cell_10_out_8),
    .out_9(n4_bit_memory_cell_10_out_9), .out_10(n4_bit_memory_cell_10_out_10),
    .out_11(n4_bit_memory_cell_10_out_11), .Col(memorycol_1_out_5), .in_3(in_5), .in_4(in_6), .in_5(in_7),
    .in_6(in_8));
  _4_bit_Memory_Cell u_4_bit_memory_cell_11 (
    .Row(memoryrow_1_out_5), .Write_Enable(in_9), .out_8(n4_bit_memory_cell_11_out_8),
    .out_9(n4_bit_memory_cell_11_out_9), .out_10(n4_bit_memory_cell_11_out_10),
    .out_11(n4_bit_memory_cell_11_out_11), .Col(memorycol_1_out_5), .in_3(in_5), .in_4(in_6), .in_5(in_7),
    .in_6(in_8));
  _4_bit_Memory_Cell u_4_bit_memory_cell_12 (
    .Row(memoryrow_1_out_6), .Write_Enable(in_9), .out_8(n4_bit_memory_cell_12_out_8),
    .out_9(n4_bit_memory_cell_12_out_9), .out_10(n4_bit_memory_cell_12_out_10),
    .out_11(n4_bit_memory_cell_12_out_11), .Col(memorycol_1_out_5), .in_3(in_5), .in_4(in_6), .in_5(in_7),
    .in_6(in_8));
  _4_bit_Memory_Cell u_4_bit_memory_cell_13 (
    .Row(memoryrow_1_out_3), .Write_Enable(in_9), .out_8(n4_bit_memory_cell_13_out_8),
    .out_9(n4_bit_memory_cell_13_out_9), .out_10(n4_bit_memory_cell_13_out_10),
    .out_11(n4_bit_memory_cell_13_out_11), .Col(memorycol_1_out_6), .in_3(in_5), .in_4(in_6), .in_5(in_7),
    .in_6(in_8));
  _4_bit_Memory_Cell u_4_bit_memory_cell_14 (
    .Row(memoryrow_1_out_4), .Write_Enable(in_9), .out_8(n4_bit_memory_cell_14_out_8),
    .out_9(n4_bit_memory_cell_14_out_9), .out_10(n4_bit_memory_cell_14_out_10),
    .out_11(n4_bit_memory_cell_14_out_11), .Col(memorycol_1_out_6), .in_3(in_5), .in_4(in_6), .in_5(in_7),
    .in_6(in_8));
  _4_bit_Memory_Cell u_4_bit_memory_cell_15 (
    .Row(memoryrow_1_out_5), .Write_Enable(in_9), .out_8(n4_bit_memory_cell_15_out_8),
    .out_9(n4_bit_memory_cell_15_out_9), .out_10(n4_bit_memory_cell_15_out_10),
    .out_11(n4_bit_memory_cell_15_out_11), .Col(memorycol_1_out_6), .in_3(in_5), .in_4(in_6), .in_5(in_7),
    .in_6(in_8));
  _4_bit_Memory_Cell u_4_bit_memory_cell_16 (
    .Row(memoryrow_1_out_6), .Write_Enable(in_9), .out_8(n4_bit_memory_cell_16_out_8),
    .out_9(n4_bit_memory_cell_16_out_9), .out_10(n4_bit_memory_cell_16_out_10),
    .out_11(n4_bit_memory_cell_16_out_11), .Col(memorycol_1_out_6), .in_3(in_5), .in_4(in_6), .in_5(in_7),
    .in_6(in_8));
  MemoryCol memorycol_1 (
    .c(in_3), .d(in_4), .out_3(memorycol_1_out_3), .out_4(memorycol_1_out_4), .out_5(memorycol_1_out_5),
    .out_6(memorycol_1_out_6));
  or or_1 (out_10, n4_bit_memory_cell_1_out_8, n4_bit_memory_cell_5_out_8, n4_bit_memory_cell_9_out_8, n4_bit_memory_cell_13_out_8, n4_bit_memory_cell_2_out_8, n4_bit_memory_cell_6_out_8, n4_bit_memory_cell_10_out_8, n4_bit_memory_cell_14_out_8, n4_bit_memory_cell_3_out_8, n4_bit_memory_cell_7_out_8, n4_bit_memory_cell_11_out_8, n4_bit_memory_cell_15_out_8, n4_bit_memory_cell_4_out_8, n4_bit_memory_cell_8_out_8, n4_bit_memory_cell_12_out_8, n4_bit_memory_cell_16_out_8);
  or or_2 (out_11, n4_bit_memory_cell_1_out_9, n4_bit_memory_cell_5_out_9, n4_bit_memory_cell_9_out_9, n4_bit_memory_cell_13_out_9, n4_bit_memory_cell_2_out_9, n4_bit_memory_cell_6_out_9, n4_bit_memory_cell_10_out_9, n4_bit_memory_cell_14_out_9, n4_bit_memory_cell_3_out_9, n4_bit_memory_cell_7_out_9, n4_bit_memory_cell_11_out_9, n4_bit_memory_cell_15_out_9, n4_bit_memory_cell_4_out_9, n4_bit_memory_cell_8_out_9, n4_bit_memory_cell_12_out_9, n4_bit_memory_cell_16_out_9);
  or or_3 (out_12, n4_bit_memory_cell_1_out_10, n4_bit_memory_cell_5_out_10, n4_bit_memory_cell_9_out_10, n4_bit_memory_cell_13_out_10, n4_bit_memory_cell_2_out_10, n4_bit_memory_cell_6_out_10, n4_bit_memory_cell_10_out_10, n4_bit_memory_cell_14_out_10, n4_bit_memory_cell_3_out_10, n4_bit_memory_cell_7_out_10, n4_bit_memory_cell_11_out_10, n4_bit_memory_cell_15_out_10, n4_bit_memory_cell_4_out_10, n4_bit_memory_cell_8_out_10, n4_bit_memory_cell_12_out_10, n4_bit_memory_cell_16_out_10);
  or or_4 (out_13, n4_bit_memory_cell_1_out_11, n4_bit_memory_cell_5_out_11, n4_bit_memory_cell_9_out_11, n4_bit_memory_cell_13_out_11, n4_bit_memory_cell_2_out_11, n4_bit_memory_cell_6_out_11, n4_bit_memory_cell_10_out_11, n4_bit_memory_cell_14_out_11, n4_bit_memory_cell_3_out_11, n4_bit_memory_cell_7_out_11, n4_bit_memory_cell_11_out_11, n4_bit_memory_cell_15_out_11, n4_bit_memory_cell_4_out_11, n4_bit_memory_cell_8_out_11, n4_bit_memory_cell_12_out_11, n4_bit_memory_cell_16_out_11);
endmodule
